# Fritzing sketch buzzer (saved by Fritzing 1.0.6)
breadboards: 1

parts:
  Arduino = Arduino Uno (Rev3)
  R1 = Resistor [tolerance=±5% resistance=220 package="0402 [SMD]"]
  J1 = Piezo Speaker

nets (from the breadboard view):
  N1: Arduino.D9_PWM, R1.Pin_0
  N2: Arduino.GND, J1.pin1
  N3: R1.Pin_1, J1.pin2
