# Fritzing sketch potentiometer_with_LED (saved by Fritzing 0.9.10b)
breadboards: 1

parts:
  Arduino = Arduino Uno (Rev3)
  U2 = POT [knob_status=50% power=0.5W package=pot_mammoth]
  LED1 = LED - 5mm [color="Red (633nm)" current=0.030 package="5 mm [THT]"]

nets:
  N1: Arduino.A2, U2.A
  N2: Arduino.D11_PWM/MOSI, LED1.anode
  N3: Arduino.5V, U2.S
  N4: Arduino.GND, U2.E, LED1.cathode
