# Fritzing sketch fade LED PWM (saved by Fritzing 0.9.10b)
breadboards: 1

parts:
  Arduino1 = Arduino Uno (Rev3)
  R2 = Resistor [tolerance=±5% resistance=220 package="0402 [SMD]"]
  LED2 = LED - 5mm [color="Red (633nm)" current=0.030 package="5 mm [THT]"]

nets:
  N1: Arduino1.D11_PWM/MOSI, R2.Pin_0
  N2: Arduino1.GND, LED2.cathode
  N3: R2.Pin_1, LED2.anode
