# Fritzing sketch traffic-light (saved by Fritzing 0.9.10b)
breadboards: 1

parts:
  Arduino = Arduino Uno (Rev3)
  LED1 = smd LED [color="Red (633nm)" package="1206 [SMD]"]
  LED2 = smd LED [color="Green (555nm)" package="1206 [SMD]"]
  LED3 = smd LED [color="Yellow (595nm)" package="1206 [SMD]"]
  R1 = Resistor [tolerance=±5% resistance=220 package="0402 [SMD]"]
  J1 = Piezo Speaker

nets:
  N1: Arduino.D11_PWM/MOSI, J1.pin2
  N2: Arduino.GND, R1.Pin_0
  N3: Arduino.D2, LED3.anode
  N4: Arduino.D3_PWM, LED2.anode
  N5: Arduino.D4, LED1.anode
  N6: LED1.cathode, LED2.cathode, LED3.cathode, R1.Pin_1
