# Fritzing sketch blink-LED (saved by Fritzing 0.9.10b)
breadboards: 1

parts:
  Arduino = Arduino Uno (Rev3)
  R1 = Resistor [tolerance=±5% resistance=220 package="0402 [SMD]"]
  LED1 = LED - 5mm [color="Red (633nm)" current=0.030 package="5 mm [THT]"]

nets:
  N1: Arduino.D11_PWM/MOSI, R1.Pin_0
  N2: Arduino.GND, LED1.cathode
  N3: R1.Pin_1, LED1.anode
