# Fritzing sketch potentiometer (saved by Fritzing 0.9.10b)
breadboards: 1

parts:
  Arduino = Arduino Uno (Rev3)
  U2 = POT [knob_status=50% power=0.5W package=pot_mammoth]

nets:
  N1: Arduino.A2, U2.A
  N2: Arduino.5V, U2.S
  N3: Arduino.GND, U2.E
