# Fritzing sketch temp_sensor (saved by Fritzing 0.9.10b)
breadboards: 1

parts:
  Arduino = Arduino Uno (Rev3)
  RHT1 = Humidity and Temperature Sensor RHT03

nets:
  N1: Arduino.D2, RHT1.Data-signal
  5V: Arduino.5V, RHT1.Vcc
  N2: Arduino.GND, RHT1.GND_2
